# Fritzing sketch Scematic (saved by Fritzing 0.8.7b)
breadboards: 1

parts:
  M5Stack = M5Stack Core (Back)
  MT3608 = Mini-360 DC-DC Buck converter [package=THT]
  part = LM324 [package=dil16]
  VCC1 = Battery
  J1 = Basic Force Sensing Resistor (FSR) [part_number=FSR package=THT]
  R1 = Resistor [tolerance=±5% resistance=10k package="0603 [SMD]"]
  R2 = Resistor [tolerance=±5% resistance=470k package="0603 [SMD]"]
  0_032uF = Capacitor [package=cap-pth-small2]
  HS-55 = Basic Servo

nets:
  GND: M5Stack.Gnd, part.GND, R1.Pin_0, 0_032uF.1
  N1: M5Stack.5V, J1.pin_0
  N2: M5Stack.35, R2.Pin_0, 0_032uF.2
  N3: M5Stack.26, HS-55.pulse
  N4: MT3608.IN-, VCC1.+
  N5: MT3608.IN+, VCC1.-
  N6: MT3608.OUT+, part.V+, HS-55.vcc
  N7: MT3608.OUT-, HS-55.gnd
  N8: part.OUT3, part.IN3-, R2.Pin_1
  N9: part.IN3+, J1.pin_1, R1.Pin_1

custom parts:
  M5Stack Core (Back): M5Stack ESP32 development kit
  Mini-360 DC-DC Buck converter: Mini-360 DC-DC Buck converter. Tiny buck step down voltage converter, input voltage 4.75 to 23V output 1 to 17V adjustable. Available from ebay and the like.
  LM324: LM324 Quad OpAmp
